# Fritzing sketch luxtronik-esphome (saved by Fritzing 0.9.3b)
breadboards: 1

parts:
  U1 = NodeMCU V3.0
  Bauteil1 = MAX3232

nets:
  N1: U1.D2, Bauteil1.RXD
  3V3: U1.D4, U1.3V3, Bauteil1.VCC, Bauteil1.TXD
  GND: U1.GND, Bauteil1.GND

custom parts:
  NodeMCU V3.0: ESP8266 based NodeMCU
  MAX3232: A random MAX3232 Breakout Board from AliExpress (RS232-TTL-Converter)
